# Fritzing sketch Montage capteur cardio (saved by Fritzing 0.9.3b)
breadboards: 2

parts:
  Arduino_Uno = Arduino Uno (Rev3)
  IC1 = LM324 [package=dil16]
  R1 = Resistor [tolerance=±5% resistance=220 package=THT]
  LED1 = Super Flux LED blue [color=Blue]
  P1 = S1133 Si Photodiode [package="8mm Ceramic [THT]"]
  R2 = Resistor [tolerance=±5% resistance=39k package=THT]
  C1 = Tantalum Capacitor [capacitance=1μF package="100 mil [THT, tantalum]"]
  R3 = Resistor [tolerance=±5% resistance=68k package=THT]
  R4 = Resistor [tolerance=±5% resistance=8.2k package=THT]
  C2 = Ceramic Capacitor [capacitance=100nF package="100 mil [THT, multilayer]"]
  C3 = Tantalum Capacitor [capacitance=1μF package="100 mil [THT, tantalum]"]
  R5 = Resistor [tolerance=±5% resistance=68k package=THT]
  C4 = Ceramic Capacitor [capacitance=100nF package="100 mil [THT, multilayer]"]
  R6 = Resistor [tolerance=±5% resistance=470k package=THT]
  R7 = Resistor [tolerance=±5% resistance=1.8k package=THT]
  Q1 = NPN-Transistor [package="SOT-23 [SMD]"]
  LED2 = LED - 5mm [color="Red (633nm)" package="5 mm [THT]"]
  LED3 = LED - 5mm [color="Red (633nm)" package="5 mm [THT]"]
  LED4 = LED - 5mm [color="Red (633nm)" package="5 mm [THT]"]
  LED5 = LED - 5mm [color="Red (633nm)" package="5 mm [THT]"]
  LED6 = LED - 5mm [color="Red (633nm)" package="5 mm [THT]"]
  LED7 = LED - 5mm [color="Red (633nm)" package="5 mm [THT]"]
  LED8 = LED - 5mm [color="Red (633nm)" package="5 mm [THT]"]
  LED9 = LED - 5mm [color="Red (633nm)" package="5 mm [THT]"]
  LED10 = LED - 5mm [color="Red (633nm)" package="5 mm [THT]"]
  LED11 = LED - 5mm [color="Red (633nm)" package="5 mm [THT]"]
  R8 = Resistor [tolerance=±5% resistance=220 package="1206 [SMD]"]
  R9 = Resistor [tolerance=±5% resistance=220 package="1206 [SMD]"]
  R10 = Resistor [tolerance=±5% resistance=220 package="1206 [SMD]"]
  R11 = Resistor [tolerance=±5% resistance=220 package="1206 [SMD]"]
  R12 = Resistor [tolerance=±5% resistance=220 package="1206 [SMD]"]
  R13 = Resistor [tolerance=±5% resistance=220 package="1206 [SMD]"]
  R14 = Resistor [tolerance=±5% resistance=220 package="1206 [SMD]"]
  R15 = Resistor [tolerance=±5% resistance=220 package="1206 [SMD]"]
  R16 = Resistor [tolerance=±5% resistance=220 package="1206 [SMD]"]
  R17 = Resistor [tolerance=±5% resistance=220 package="1206 [SMD]"]

nets:
  N1: Arduino_Uno.A0, Q1.2
  N2: Arduino_Uno.D8, LED9.cathode
  N3: Arduino_Uno.D9_PWM, LED7.cathode
  N4: Arduino_Uno.D10_PWM/SS, LED8.cathode
  N5: Arduino_Uno.D11_PWM/MOSI, LED10.cathode
  GND: Arduino_Uno.GND, IC1.GND, LED1.cathode, P1.anode, R3.Pin_1, R4.Pin_1, R5.Pin_1
  N6: Arduino_Uno.D2, LED5.cathode
  N7: Arduino_Uno.D3_PWM, LED3.cathode
  N8: Arduino_Uno.D4, LED2.cathode
  N9: Arduino_Uno.D5_PWM, LED4.cathode
  N10: Arduino_Uno.D6_PWM, LED6.cathode
  N11: Arduino_Uno.D7, LED11.cathode
  N12: Arduino_Uno.5V, IC1.V+, R1.Pin_0, R2.Pin_0, Q1.1
  N13: IC1.OUT1, C2.1, C3.+
  N14: IC1.IN1-, R4.Pin_0, C2.0
  N15: IC1.IN1+, C1.-, R3.Pin_0
  N16: IC1.IN4+, C3.-, R5.Pin_0
  N17: IC1.IN4-, C4.0, R6.Pin_1
  N18: IC1.OUT4, C4.1, R6.Pin_0, R7.Pin_0
  N19: R1.Pin_1, LED1.anode
  N20: P1.cathode, R2.Pin_1, C1.+
  N21: R7.Pin_1, Q1.0
  N22: LED2.anode, R8.Pin_1
  N23: LED3.anode, R9.Pin_1
  N24: LED4.anode, R11.Pin_1
  N25: LED5.anode, R10.Pin_1
  N26: LED6.anode, R12.Pin_1
  N27: LED7.anode, R15.Pin_0
  N28: LED8.anode, R14.Pin_0
  N29: LED9.anode, R16.Pin_0
  N30: LED10.anode, R13.Pin_0
  N31: LED11.anode, R17.Pin_0
  N32: R8.Pin_0, R10.Pin_0, R11.Pin_0
  N33: R13.Pin_1, R15.Pin_1, R16.Pin_1

custom parts:
  LM324: LM324 Quad OpAmp
