# Fritzing sketch Montage capteur cardio (saved by Fritzing 0.9.3b)
breadboards: 2

parts:
  IC1 = LM324 [package=dil16]
  R1 = Resistor [tolerance=±5% resistance=220 package=THT]
  LED1 = Super Flux LED blue [color=Blue]
  P1 = S1133 Si Photodiode [package="8mm Ceramic [THT]"]
  R2 = Resistor [tolerance=±5% resistance=39k package=THT]
  C1 = Tantalum Capacitor [capacitance=1μF package="100 mil [THT, tantalum]"]
  R3 = Resistor [tolerance=±5% resistance=68k package=THT]
  R4 = Resistor [tolerance=±5% resistance=8.2k package=THT]
  C2 = Ceramic Capacitor [capacitance=100nF package="100 mil [THT, multilayer]"]
  C3 = Tantalum Capacitor [capacitance=1μF package="100 mil [THT, tantalum]"]
  R5 = Resistor [tolerance=±5% resistance=68k package=THT]
  C4 = Ceramic Capacitor [capacitance=100nF package="100 mil [THT, multilayer]"]
  R6 = Resistor [tolerance=±5% resistance=470k package=THT]
  R7 = Resistor [tolerance=±5% resistance=1.8k package=THT]
  Q1 = NPN-Transistor [package="SOT-23 [SMD]"]
  LED2 = LED - 5mm [color="Red (633nm)" package="5 mm [THT]"]
  LED3 = LED - 5mm [color="Red (633nm)" package="5 mm [THT]"]
  LED4 = LED - 5mm [color="Red (633nm)" package="5 mm [THT]"]
  LED5 = LED - 5mm [color="Red (633nm)" package="5 mm [THT]"]
  LED6 = LED - 5mm [color="Red (633nm)" package="5 mm [THT]"]
  LED7 = LED - 5mm [color="Red (633nm)" package="5 mm [THT]"]
  LED8 = LED - 5mm [color="Red (633nm)" package="5 mm [THT]"]
  LED9 = LED - 5mm [color="Red (633nm)" package="5 mm [THT]"]
  LED10 = LED - 5mm [color="Red (633nm)" package="5 mm [THT]"]
  LED11 = LED - 5mm [color="Red (633nm)" package="5 mm [THT]"]
  R8 = Resistor [tolerance=±5% resistance=220 package="1206 [SMD]"]
  R9 = Resistor [tolerance=±5% resistance=220 package="1206 [SMD]"]
  R10 = Resistor [tolerance=±5% resistance=220 package="1206 [SMD]"]
  R11 = Resistor [tolerance=±5% resistance=220 package="1206 [SMD]"]
  R12 = Resistor [tolerance=±5% resistance=220 package="1206 [SMD]"]
  R13 = Resistor [tolerance=±5% resistance=220 package="1206 [SMD]"]
  R14 = Resistor [tolerance=±5% resistance=220 package="1206 [SMD]"]
  R15 = Resistor [tolerance=±5% resistance=220 package="1206 [SMD]"]
  R16 = Resistor [tolerance=±5% resistance=220 package="1206 [SMD]"]
  R17 = Resistor [tolerance=±5% resistance=220 package="1206 [SMD]"]
  Composant1 = Arduino Mega 2560 (Rev3)
  Composant2 = LCD Keypad Shield

nets:
  N1: IC1.OUT1, C2.1, C3.+
  N2: IC1.IN1-, R4.Pin_0, C2.0
  N3: IC1.IN1+, C1.-, R3.Pin_0
  5V: IC1.V+, R1.Pin_0, R2.Pin_0, Q1.1, Composant1.5V, Composant2.+5V
  GND: IC1.GND, LED1.cathode, P1.anode, R3.Pin_1, R4.Pin_1, R5.Pin_1, R8.Pin_0, R10.Pin_0, R11.Pin_0, R13.Pin_1, R15.Pin_1, R16.Pin_1, Composant1.GND, Composant2.GND
  N4: IC1.IN4+, C3.-, R5.Pin_0
  N5: IC1.IN4-, C4.0, R6.Pin_1
  N6: IC1.OUT4, C4.1, R6.Pin_0, R7.Pin_0
  N7: R1.Pin_1, LED1.anode
  N8: P1.cathode, R2.Pin_1, C1.+
  N9: R7.Pin_1, Q1.0
  N10: Q1.2, Composant1.A10
  N11: LED2.cathode, Composant1.D32
  N12: LED2.anode, R8.Pin_1
  N13: LED3.cathode, Composant1.D31
  N14: LED3.anode, R9.Pin_1
  N15: LED4.cathode, Composant1.D33
  N16: LED4.anode, R11.Pin_1
  N17: LED5.cathode, Composant1.D30
  N18: LED5.anode, R10.Pin_1
  N19: LED6.cathode, Composant1.D34
  N20: LED6.anode, R12.Pin_1
  N21: LED7.cathode, Composant1.D37
  N22: LED7.anode, R15.Pin_0
  N23: LED8.cathode, Composant1.D38
  N24: LED8.anode, R14.Pin_0
  N25: LED9.cathode, Composant1.D36
  N26: LED9.anode, R16.Pin_0
  N27: LED10.cathode, Composant1.D39
  N28: LED10.anode, R13.Pin_0
  N29: LED11.cathode, Composant1.D35
  N30: LED11.anode, R17.Pin_0
  N31: Composant1.A1, Composant2.A1
  N32: Composant1.A2, Composant2.A2
  N33: Composant1.A3, Composant2.A3
  N34: Composant1.A4, Composant2.A4(SDA)
  N35: Composant1.A5, Composant2.A5(CLK)
  N36: Composant1.RESET, Composant2.RESET
  3V3: Composant1.3V3, Composant2.+3V3
  VIN: Composant1.VIN, Composant2.VIN
  N37: Composant1.D1_TX0, Composant2.D0_RX
  N38: Composant1.D2_PWM, Composant2.D1_TX
  N39: Composant1.D3_PWM, Composant2.D2
  N40: Composant1.D4_PWM, Composant2.D3
  N41: Composant1.D5_PWM, Composant2.D11_MOSI
  N42: Composant1.D6_PWM, Composant2.D12_MISO
  N43: Composant1.D7_PWM, Composant2.D13_SCK

custom parts:
  LM324: LM324 Quad OpAmp
  LCD Keypad Shield: It consists of a 1602 white character blue backlight LCD. The keypad consists of 5 keys — select, up, right, down and left. To save the digital IO pins, the keypad interface uses only one ADC channel. The key value is read through a 5 stage voltage divider.
